// Logisim project ex1.circ as structural Verilog: 5 circuits, main circuit NAND1
module NAND1 (
  input  A,
  input  B,
  output RESULT
);

  wire not_1_out, not_2_out;

  not not_1 (not_1_out, A);
  not not_2 (not_2_out, B);
  or or_1 (RESULT, not_1_out, not_2_out);

  // Notes on the sheet:
  //   PUT CIRCUITRY HERE
endmodule

module NOR1 (
  input  A,
  input  B,
  output RESULT
);

  wire not_1_out, not_2_out;

  not not_1 (not_1_out, A);
  not not_2 (not_2_out, B);
  and and_1 (RESULT, not_1_out, not_2_out);

  // Notes on the sheet:
  //   PUT CIRCUITRY HERE
endmodule

module XOR1 (
  input  A,
  input  B,
  output RESULT
);

  wire nand1_1_result, or_1_out;

  NAND1 nand1_1 (.A(A), .B(B), .RESULT(nand1_1_result));
  or or_1 (or_1_out, A, B);
  and and_1 (RESULT, nand1_1_result, or_1_out);

  // Notes on the sheet:
  //   PUT CIRCUITRY HERE
endmodule

module MUX2 (
  input  A,
  input  B,
  input  Sel,
  output out_4,
  output RESULT
);

  wire and_1_out, and_2_out, not_1_out;

  and and_1 (and_1_out, A, not_1_out);
  not not_1 (not_1_out, Sel);
  and and_2 (and_2_out, B, Sel);
  or or_1 (out_4, and_1_out, and_2_out);

  // Notes on the sheet:
  //   PUT CIRCUITRY HERE
endmodule

module MUX4 (
  input  A,
  input  B,
  input  C,
  input  D,
  input  Sel1,
  input  Sel2,
  output RESULT
);

  wire mux2_1_out_4, mux2_2_out_4;

  MUX2 mux2_1 (.A(A), .B(B), .Sel(Sel1), .out_4(mux2_1_out_4));  // open: RESULT
  MUX2 mux2_2 (.A(C), .B(D), .Sel(Sel1), .out_4(mux2_2_out_4));  // open: RESULT
  MUX2 mux2_3 (.A(mux2_1_out_4), .B(mux2_2_out_4), .Sel(Sel2), .out_4(RESULT));  // open: RESULT

  // Notes on the sheet:
  //   PUT CIRCUITRY HERE
endmodule
