// Logisim project ex4.circ as structural Verilog: 1 circuit, main circuit Split
module Split (
  input  [7:0] In1,
  output Out1,
  output [7:0] Out2
);

  wire [7:7] not_1_out;

  not not_1 (not_1_out[7], In1[7]);
  and and_1 (Out1, In1[0], In1[7]);
  Bit_Extender #(.out_width(8)) bit_extender_1 (.in({not_1_out[7], In1[6:0]}), .out(Out2));

  // Notes on the sheet:
  //   PUT CIRCUITRY HERE
  //   Answer: negative odd interger will make Out1=1
endmodule
