// Logisim project ex5.circ as structural Verilog: 5 circuits, main circuit rotr
module rotr (
  input  [7:0] in_1,
  input  [15:0] A,
  input  [3:0] in_3,
  input  [1:0] in_4,
  input  [3:0] B,
  input  in_6,
  output [7:0] out_7,
  output [15:0] Out1,
  output [7:0] out_9,
  output [3:0] out_10,
  output [1:0] out_11,
  output out_12
);

  wire [6:0] undriven;

  Multiplexer #(.width(8), .enable("false")) multiplexer_1 (.in0(A[15:8]), .in1(in_1), .out(out_7), .sel(B[3]));
  Multiplexer #(.width(8), .enable("false")) multiplexer_2 (.in0(A[7:0]), .in1(A[15:8]), .out(out_9), .sel(B[3]));
  Multiplexer #(.width(4), .enable("false")) multiplexer_3 (.in0(undriven[3:0]), .in1(in_3), .out(out_10), .sel(B[2]));
  Multiplexer #(.width(2), .enable("false")) multiplexer_4 (.in0(undriven[5:4]), .in1(in_4), .out(out_11), .sel(B[1]));
  Multiplexer #(.enable("false")) multiplexer_5 (.in0(undriven[6]), .in1(in_6), .out(out_12), .sel(B[0]));

  // Other names for the same wires on the sheet: B1 = B[0]; B2 = B[1]; B4 = B[2]; B8 = B[3]

  // Notes on the sheet:
  //   PUT CIRCUITRY HERE
endmodule

module rot8 (
  input  [15:0] in_1,
  output [15:0] out_2
);


  // Notes on the sheet:
  //   PUT CIRCUITRY HERE
endmodule

module rot4 (
  input  [15:0] in_1,
  output [15:0] out_2
);


  // Notes on the sheet:
  //   PUT CIRCUITRY HERE
endmodule

module rot2 (
  input  [15:0] in_1,
  output [15:0] out_2
);


  // Notes on the sheet:
  //   PUT CIRCUITRY HERE
endmodule

module rot1 (
  input  [15:0] in_1,
  output [15:0] out_2
);


  // Notes on the sheet:
  //   PUT CIRCUITRY HERE
endmodule
